# Fritzing sketch Breadboard (saved by Fritzing 0.9.4)
breadboards: 1

parts:
  Raspberry_Pi1 = Raspberry Pi B rev2
  LED2 = smd LED [color="Red (633nm)" package="0603 [SMD]"]
  LED1 = smd LED [color="Green (565nm)" package="0603 [SMD]"]
  R1 = Resistor [tolerance=±5% resistance=330 package="0805 [SMD]"]
  R2 = Resistor [tolerance=±5% resistance=330 package="0805 [SMD]"]
  S1 = Momentary Switch [package=ksa_sealed_tac_switch]

nets:
  N1: Raspberry_Pi1.3V3, S1.2
  N2: Raspberry_Pi1.GND, R1.Pin_0, R2.Pin_0
  N3: Raspberry_Pi1.GPIO_18, LED1.anode
  N4: Raspberry_Pi1.GPIO_24, LED2.anode
  N5: Raspberry_Pi1.GPIO_25, S1.4
  N6: LED2.cathode, R2.Pin_1
  N7: LED1.cathode, R1.Pin_1

notes:
  PWM
  Relay Output
  Relay Input
